# Fritzing sketch scheme (saved by Fritzing 0.8.7b)
circuit board: 8.46667cm x 5.64444cm
breadboards: 1

parts:
  Часть1 = Arduino Uno (Rev3)
  S1 = Pushbutton [package="[THT]"]
  R1 = Resistor [tolerance=±5% resistance=10k package=THT]
  R2 = Resistor [tolerance=±5% resistance=220 package=THT]
  LED1 = LED - 5mm [color="Red (633nm)" package="5 mm [THT]"]

nets:
  N1: Часть1.D8, S1.Pin_1, S1.Pin_2, R1.Pin_0
  N2: Часть1.D13/SCK, R2.Pin_1
  N3: Часть1.5V, S1.Pin_3, S1.Pin_4
  N4: Часть1.GND, R1.Pin_1, LED1.cathode
  N5: R2.Pin_0, LED1.anode
