# Fritzing sketch scheme (saved by Fritzing 0.8.7b)
breadboards: 1

parts:
  Часть1 = Arduino Uno (Rev3)
  R1 = Resistor [tolerance=±5% resistance=220 package=THT]
  LED1 = LED - 5mm [color="Red (633nm)" package="5 mm [THT]"]

nets:
  N1: Часть1.D11_PWM/MOSI, R1.Pin_0
  N2: Часть1.GND, LED1.cathode
  N3: R1.Pin_1, LED1.anode
