# Fritzing sketch scheme (saved by Fritzing 0.8.7b)
circuit board: 8.46667cm x 5.64444cm
breadboards: 1

parts:
  R2 = Resistor [tolerance=±5% resistance=220 package=THT]
  LED1 = LED - 5mm [color="Red (633nm)" package="5 mm [THT]"]
  R3 = Rotary Potentiometer (Small) [maximum_resistance=100kΩ package=THT]
  Часть1 = Arduino Uno (Rev3)

nets:
  N1: R2.Pin_0, LED1.anode
  N2: R2.Pin_1, Часть1.D11_PWM/MOSI
  N3: LED1.cathode, R3.leg1, Часть1.GND
  N4: R3.wiper, Часть1.A0
  N5: R3.leg2, Часть1.5V
